// Digital circuit accumulator.dig as structural Verilog
module accumulator (
  input  [23:0] IN,
  input  CLK,
  input  RESET,
  output [23:0] OUT
);

  wire [23:0] ADDER_s, multiplexer_1_out;

  Register #(.Bits(24)) REGISTER (.D(multiplexer_1_out), .C(CLK), .en(1'b1), .Q(OUT));
  Add #(.Bits(24)) ADDER (.a(OUT), .b(IN), .c_i(1'b0), .s(ADDER_s));  // open: c_o
  Multiplexer #(.Bits(24)) multiplexer_1 (.sel(RESET), .in_0(ADDER_s), .in_1({24{1'b0}}), .out(multiplexer_1_out));
endmodule
