// Digital circuit accumulator_40.dig as structural Verilog
module accumulator_40 (
  input  [39:0] IN,
  input  CLK,
  input  RESET,
  output [39:0] OUT
);

  wire [39:0] ADDER_s, multiplexer_1_out;

  Register #(.Bits(40)) REGISTER (.D(multiplexer_1_out), .C(CLK), .en(1'b1), .Q(OUT));
  Add #(.Bits(40)) ADDER (.a(OUT), .b(IN), .c_i(1'b0), .s(ADDER_s));  // open: c_o
  Multiplexer #(.Bits(40)) multiplexer_1 (.sel(RESET), .in_0(ADDER_s), .in_1({40{1'b0}}), .out(multiplexer_1_out));
endmodule
