// Digital circuit dead_reckoning.dig as structural Verilog
module dead_reckoning (
  input  [15:0] OMEGA,
  input  [15:0] VELOCITY,
  input  RESET,
  input  CLK,
  output [15:0] THETA,
  output [15:0] position_X,
  output [15:0] postion_Z
);

  wire [7:0] head_1_address;
  wire [15:0] trig_1_cos, trig_1_sin;

  head head_1 (.OMEGA(OMEGA), .CLK(CLK), .RESET(RESET), .THETA(THETA), .ADDRESS(head_1_address));
  trig trig_1 (.ADDRESS(head_1_address), .SIN(trig_1_sin), .COS(trig_1_cos));
  position position_1 (
    .VELOCITY(VELOCITY), .SIN(trig_1_sin), .COS(trig_1_cos), .RESET(RESET), .CLK(CLK), .X(position_X),
    .Z(postion_Z));

  // Notes on the sheet:
  //   CLK: Hz: 32
endmodule
