// Digital circuit head.dig as structural Verilog
module head (
  input  [15:0] OMEGA,
  input  CLK,
  input  RESET,
  output [15:0] THETA,
  output [7:0] ADDRESS
);

  wire [7:0] accumulator_1_out;

  accumulator accumulator_1 (
    .IN({{9{OMEGA[15]}}, OMEGA[14:0]}), .CLK(CLK), .RESET(RESET),
    .OUT({ADDRESS, THETA[7:0], accumulator_1_out}));

  assign THETA[15:8] = ADDRESS;
endmodule
