// Digital circuit position.dig as structural Verilog
module position (
  input  [15:0] VELOCITY,
  input  [15:0] SIN,
  input  [15:0] COS,
  input  RESET,
  input  CLK,
  output [15:0] X,
  output [15:0] Z
);

  wire [31:0] MUP_A_mul, MUP_B_mul;
  wire [39:0] accumulator_40_1_out, accumulator_40_2_out;

  Mul #(.Bits(16), .Signed("true")) MUP_A (.a(VELOCITY), .b(COS), .mul(MUP_A_mul));
  Mul #(.Bits(16), .Signed("true")) MUP_B (.a(VELOCITY), .b(SIN), .mul(MUP_B_mul));
  accumulator_40 accumulator_40_1 (
    .IN({{9{MUP_A_mul[31]}}, MUP_A_mul[30:0]}), .CLK(CLK), .RESET(RESET),
    .OUT({accumulator_40_1_out[39:38], X, accumulator_40_1_out[21:0]}));
  accumulator_40 accumulator_40_2 (
    .IN({{9{MUP_B_mul[31]}}, MUP_B_mul[30:0]}), .CLK(CLK), .RESET(RESET),
    .OUT({accumulator_40_2_out[39:38], Z, accumulator_40_2_out[21:0]}));
endmodule
