// Digital circuit trig.dig as structural Verilog
module trig (
  input  [7:0] ADDRESS,
  output [15:0] SIN,
  output [15:0] COS
);

  ROM #(.bigEndian("true"), .AddrBits(8), .isProgramMemory("true"), .Bits(16)) SIN_VALUES (
    .A(ADDRESS), .sel(1'b1), .D(SIN));
  ROM #(.bigEndian("true"), .AddrBits(8), .isProgramMemory("true"), .Bits(16)) COS_VALUES (
    .A(ADDRESS), .sel(1'b1), .D(COS));

  // Notes on the sheet:
  //   SIN_VALUES loads sin_rom.hex
  //   COS_VALUES loads cos_rom.hex
endmodule
